# Fritzing sketch ESP32C3_wiring (saved by Fritzing 1.0.4)

parts:
  Part1 = SHT1x-Breakout
  A1 = XIAO ESP32C3-tht
  KF-1 = KF-301 Relay [package=THT]
  S2 = Momentary Switch [package=ksa_sealed_tac_switch]

nets:
  N1: Part1.SCK, A1.Pin_14
  N2: Part1.DATA, A1.Pin_13
  N3: Part1.VCC, A1.Pin_20
  N4: Part1.GND, A1.Pin_21, KF-1.ground, S2.2
  N5: A1.Pin_11, KF-1.signal
  N6: A1.Pin_16, S2.1
  N7: A1.Pin_22, KF-1.power

custom parts:
  XIAO ESP32C3-tht: Seeed Studio XIAO ESP32C3 adopts new RISC-V architecture, supporting both Wi-Fi and BLE wireless connectivities.
  KF-301 Relay: KF-301
